# Fritzing sketch Timer_Diagramm (saved by Fritzing 0.9.4)
breadboards: 1

parts:
  LCD1 = LCD screen  # not connected
  Part1 = Arduino Uno (Rev3)
  S1 = Pushbutton [package="[THT]"]
  S2 = Pushbutton [package="[THT]"]
  S3 = Pushbutton [package="[THT]"]
  LED1 = LED - 5mm [color="Green (555nm)" package="5 mm [THT]"]
  LED3 = LED - 5mm [color="Red (633nm)" package="5 mm [THT]"]
  LED2 = smd LED [color="Blue (430nm)" package="0603 [SMD]"]
  R1 = Resistor [tolerance=±5% resistance=220 package=THT]
  R2 = Resistor [tolerance=±5% resistance=220 package=THT]
  R3 = Resistor [tolerance=±5% resistance=220 package=THT]
  R4 = Resistor [tolerance=±5% resistance=220 package=THT]
  R5 = Resistor [tolerance=±5% resistance=220 package=THT]
  R6 = Resistor [tolerance=±5% resistance=220 package=THT]

nets:
  N1: Part1.D10_PWM/SS, S1.Pin_1, S1.Pin_2, R6.Pin_0
  N2: Part1.D11_PWM/MOSI, LED1.cathode
  N3: Part1.D12/MISO, LED3.cathode
  N4: Part1.D1/TX, LED2.cathode
  N5: Part1.D2, S2.Pin_1, S2.Pin_2, R4.Pin_0
  N6: Part1.D3_PWM, S3.Pin_1, S3.Pin_2, R5.Pin_0
  N7: Part1.5V, S1.Pin_3, S1.Pin_4, S2.Pin_3, S2.Pin_4, S3.Pin_3, S3.Pin_4
  N8: Part1.GND, R1.Pin_1, R2.Pin_1, R3.Pin_1, R4.Pin_1, R5.Pin_1, R6.Pin_1
  N9: LED1.anode, R2.Pin_0
  N10: LED3.anode, R3.Pin_0
  N11: LED2.anode, R1.Pin_0
